// Logisim project T-21-s1-logisim (1).circ as structural Verilog: 1 circuit, main circuit main
module main (
);

  wire _0_out, _1_out, _2_out, _3_out, _4_out, _5_out, _6_out, _7_out, _8_out, _9_out, and_1_out, and_2_out,
       and_3_out, and_4_out, and_5_out, and_6_out, and_7_out, and_8_out, and_9_out, and_10_out, and_11_out,
       and_12_out, and_13_out, and_14_out, and_15_out, and_16_out, and_17_out, and_18_out, and_19_out,
       and_20_out, and_21_out, and_22_out, and_23_out, and_24_out, and_25_out, and_26_out, button_1_out,
       button_2_out, button_3_out, d_ff_1_q, not_1_out, not_2_out, or_1_out, or_2_out, or_3_out, or_4_out,
       or_5_out, or_6_out, or_7_out, shift_register_1_q0, shift_register_1_q1, shift_register_1_q2,
       shift_register_1_q3, shift_register_2_q0, shift_register_2_q1, shift_register_2_q2,
       shift_register_2_q3, shift_register_3_q0, shift_register_3_q1, shift_register_3_q2,
       shift_register_3_q3, shift_register_4_q0, shift_register_4_q1, shift_register_4_q2,
       shift_register_4_q3, shift_register_5_q0, shift_register_5_q1, shift_register_5_q2,
       shift_register_5_q3, shift_register_6_q0, shift_register_6_q1, shift_register_6_q2,
       shift_register_6_q3, shift_register_7_q0, shift_register_7_q1, shift_register_7_q2,
       shift_register_7_q3, shift_register_8_q0, shift_register_8_q1, shift_register_8_q2,
       shift_register_8_q3, shift_register_9_out, t_ff_1_q, t_ff_2_q, t_ff_3_q, xnor_1_out, xnor_2_out,
       xnor_3_out, xnor_4_out, xnor_5_out, xnor_6_out, xnor_7_out, xnor_8_out, xnor_9_out, xnor_10_out,
       xnor_11_out, xnor_12_out, xnor_13_out, xnor_14_out, xnor_15_out, xnor_16_out;

  Button button_1 (.out(button_1_out));
  Button button_2 (.out(button_2_out));
  Button button_3 (.out(button_3_out));
  T_Flip_Flop t_ff_1 (.clk(button_1_out), .T(1'b1), .Q(t_ff_1_q));  // open: Qn, preset, reset, en
  T_Flip_Flop t_ff_2 (.clk(button_3_out), .T(1'b1), .Q(t_ff_2_q));  // open: Qn, preset, reset, en
  Button _0 (.out(_0_out));
  Button _1 (.out(_1_out));
  Button _2 (.out(_2_out));
  Button _3 (.out(_3_out));
  Button _4 (.out(_4_out));
  Button _5 (.out(_5_out));
  Button _6 (.out(_6_out));
  Button _7 (.out(_7_out));
  Button _8 (.out(_8_out));
  Button _9 (.out(_9_out));
  and and_1 (and_1_out, t_ff_1_q, button_1_out);
  or or_1 (or_1_out, button_2_out, button_3_out);
  and and_2 (and_2_out, t_ff_2_q, _0_out);
  and and_3 (and_3_out, t_ff_2_q, _1_out);
  and and_4 (and_4_out, t_ff_2_q, _2_out);
  and and_5 (and_5_out, t_ff_2_q, _3_out);
  and and_6 (and_6_out, t_ff_2_q, _4_out);
  and and_7 (and_7_out, t_ff_2_q, _5_out);
  and and_8 (and_8_out, t_ff_2_q, _6_out);
  and and_9 (and_9_out, t_ff_2_q, _7_out);
  and and_10 (and_10_out, t_ff_2_q, _8_out);
  and and_11 (and_11_out, t_ff_2_q, _9_out);
  and and_12 (and_12_out, t_ff_2_q, button_3_out);
  and and_13 (and_13_out, button_2_out, t_ff_2_q);
  or or_2 (or_2_out, and_3_out, and_5_out, and_7_out, and_9_out, and_11_out);
  or or_3 (or_3_out, and_2_out, and_4_out, and_5_out, and_8_out, and_9_out);
  or or_4 (or_4_out, and_6_out, and_7_out, and_8_out, and_9_out);
  or or_5 (or_5_out, and_2_out, and_10_out, and_11_out);
  or or_6 (or_6_out, and_2_out, and_3_out, and_4_out, and_5_out, and_6_out, and_7_out, and_8_out, and_9_out, and_10_out, and_11_out);
  Shift_Register #(.length(4)) shift_register_1 (
    .in(or_2_out), .clk(or_6_out), .clr(or_1_out), .q0(shift_register_1_q0), .q1(shift_register_1_q1),
    .q2(shift_register_1_q2), .q3(shift_register_1_q3));  // open: shift, out, load, d0, d1, d2, d3
  Shift_Register #(.length(4)) shift_register_2 (
    .in(or_3_out), .clk(or_6_out), .clr(or_1_out), .q0(shift_register_2_q0), .q1(shift_register_2_q1),
    .q2(shift_register_2_q2), .q3(shift_register_2_q3));  // open: shift, out, load, d0, d1, d2, d3
  Shift_Register #(.length(4)) shift_register_3 (
    .in(or_4_out), .clk(or_6_out), .clr(or_1_out), .q0(shift_register_3_q0), .q1(shift_register_3_q1),
    .q2(shift_register_3_q2), .q3(shift_register_3_q3));  // open: shift, out, load, d0, d1, d2, d3
  Shift_Register #(.length(4)) shift_register_4 (
    .in(or_5_out), .clk(or_6_out), .clr(or_1_out), .q0(shift_register_4_q0), .q1(shift_register_4_q1),
    .q2(shift_register_4_q2), .q3(shift_register_4_q3));  // open: shift, out, load, d0, d1, d2, d3
  or or_7 (or_7_out, shift_register_4_q0, shift_register_3_q0, shift_register_2_q0, shift_register_1_q0);
  and and_14 (and_14_out, button_3_out, ~t_ff_2_q);  // AND_Gate
  xnor xnor_1 (xnor_1_out, shift_register_1_q1, shift_register_5_q1);
  xnor xnor_2 (xnor_2_out, shift_register_1_q0, shift_register_5_q0);
  and and_15 (and_15_out, xnor_2_out, xnor_1_out, xnor_9_out, xnor_10_out);
  xnor xnor_3 (xnor_3_out, shift_register_2_q1, shift_register_6_q1);
  xnor xnor_4 (xnor_4_out, shift_register_2_q0, shift_register_6_q0);
  and and_16 (and_16_out, xnor_4_out, xnor_3_out, xnor_12_out, xnor_11_out);
  xnor xnor_5 (xnor_5_out, shift_register_3_q1, shift_register_8_q1);
  xnor xnor_6 (xnor_6_out, shift_register_3_q0, shift_register_8_q0);
  and and_17 (and_17_out, xnor_6_out, xnor_5_out, xnor_13_out, xnor_14_out);
  xnor xnor_7 (xnor_7_out, shift_register_4_q1, shift_register_7_q1);
  xnor xnor_8 (xnor_8_out, shift_register_4_q0, shift_register_7_q0);
  and and_18 (and_18_out, xnor_8_out, xnor_7_out, xnor_16_out, xnor_15_out);
  xnor xnor_9 (xnor_9_out, shift_register_1_q2, shift_register_5_q2);
  xnor xnor_10 (xnor_10_out, shift_register_1_q3, shift_register_5_q3);
  xnor xnor_11 (xnor_11_out, shift_register_2_q3, shift_register_6_q3);
  xnor xnor_12 (xnor_12_out, shift_register_2_q2, shift_register_6_q2);
  xnor xnor_13 (xnor_13_out, shift_register_3_q2, shift_register_8_q2);
  xnor xnor_14 (xnor_14_out, shift_register_3_q3, shift_register_8_q3);
  xnor xnor_15 (xnor_15_out, shift_register_4_q3, shift_register_7_q3);
  xnor xnor_16 (xnor_16_out, shift_register_4_q2, shift_register_7_q2);
  and and_19 (and_19_out, and_13_out, and_18_out, and_17_out, and_16_out, and_15_out);
  and and_20 (and_20_out, or_6_out, t_ff_3_q);
  T_Flip_Flop t_ff_3 (.clk(and_19_out), .T(1'b1), .Q(t_ff_3_q), .reset(and_14_out));  // open: Qn, preset, en
  and and_21 (and_21_out, and_19_out, ~t_ff_3_q);  // AND_Gate
  and and_22 (and_22_out, or_4_out, t_ff_3_q);
  and and_23 (and_23_out, or_5_out, t_ff_3_q);
  and and_24 (and_24_out, or_3_out, t_ff_3_q);
  and and_25 (and_25_out, or_2_out, t_ff_3_q);
  Shift_Register #(.length(4)) shift_register_5 (
    .in(and_25_out), .clk(and_20_out), .clr(and_21_out), .q0(shift_register_5_q0), .q1(shift_register_5_q1),
    .q2(shift_register_5_q2), .q3(shift_register_5_q3));  // open: shift, out, load, d0, d1, d2, d3
  Shift_Register #(.length(4)) shift_register_6 (
    .in(and_24_out), .clk(and_20_out), .clr(and_21_out), .q0(shift_register_6_q0), .q1(shift_register_6_q1),
    .q2(shift_register_6_q2), .q3(shift_register_6_q3));  // open: shift, out, load, d0, d1, d2, d3
  Shift_Register #(.length(4)) shift_register_7 (
    .in(and_23_out), .clk(and_20_out), .clr(and_21_out), .q0(shift_register_7_q0), .q1(shift_register_7_q1),
    .q2(shift_register_7_q2), .q3(shift_register_7_q3));  // open: shift, out, load, d0, d1, d2, d3
  LED Password_is_changable (.in(t_ff_3_q));
  Shift_Register #(.length(4)) shift_register_8 (
    .in(and_22_out), .clk(and_20_out), .clr(and_21_out), .q0(shift_register_8_q0), .q1(shift_register_8_q1),
    .q2(shift_register_8_q2), .q3(shift_register_8_q3));  // open: shift, out, load, d0, d1, d2, d3
  not not_1 (not_1_out, t_ff_3_q);
  and and_26 (and_26_out, not_1_out, and_15_out, and_16_out, and_17_out, and_18_out, or_7_out, button_3_out);
  not not_2 (not_2_out, and_26_out);
  Shift_Register #(.length(5)) shift_register_9 (
    .in(not_2_out), .clk(and_12_out), .out(shift_register_9_out), .clr(and_26_out));  // open: shift, load, d0, q0, d1, q1, d2, q2, d3, q3, d4, q4
  LED led_1 (.in(d_ff_1_q));
  D_Flip_Flop d_ff_1 (.clk(and_26_out), .D(1'b1), .Q(d_ff_1_q));  // open: Qn, preset, en, reset
  LED Password_is_5_times_dismatched (.in(shift_register_9_out));
endmodule
